// Logisim project CRC.circ as structural Verilog: 1 circuit, main circuit main
module main (
  input  in_1,
  input  in_2,
  input  in_3,
  input  in_4,
  input  in_5,
  input  in_6,
  input  in_7,
  input  in_8,
  input  in_9,
  input  in_10,
  input  in_11,
  input  in_12,
  input  in_13,
  output out_14,
  output out_15,
  output out_16,
  output out_17
);

  wire and_1_out, and_2_out, and_3_out, and_4_out, and_5_out, and_6_out, and_7_out, and_8_out, and_9_out,
       and_10_out, and_11_out, and_12_out, clock_1_out, d_ff_1_q, d_ff_2_q, d_ff_3_q, d_ff_8_q, d_ff_9_q,
       d_ff_10_q, d_ff_11_q, xor_2_out, xor_3_out, xor_4_out, xor_5_out;

  Clock clock_1 (.out(clock_1_out));
  D_Flip_Flop d_ff_1 (.clk(clock_1_out), .Q(d_ff_1_q), .preset(and_1_out));  // open: D, Qn, en, reset
  and and_1 (and_1_out, in_6, in_7);
  and and_2 (and_2_out, in_1, out_14);
  and and_3 (and_3_out, in_2, out_14);
  and and_4 (and_4_out, in_3, out_14);
  and and_5 (and_5_out, in_4, out_14);
  and and_6 (and_6_out, in_5, out_14);
  D_Flip_Flop d_ff_2 (.clk(clock_1_out), .D(d_ff_1_q), .Q(d_ff_2_q), .preset(and_7_out));  // open: Qn, en, reset
  and and_7 (and_7_out, d_ff_1_q, in_8);
  D_Flip_Flop d_ff_3 (.clk(clock_1_out), .D(d_ff_2_q), .Q(d_ff_3_q), .preset(and_8_out));  // open: Qn, en, reset
  and and_8 (and_8_out, d_ff_2_q, in_9);
  // XOR_Gate xor_1 has open pins: in1=out_14, in3=and_2_out, out=open
  xor xor_2 (xor_2_out, out_15, and_3_out);
  xor xor_3 (xor_3_out, and_4_out, out_16);
  xor xor_4 (xor_4_out, and_5_out, out_17);
  xor xor_5 (xor_5_out, and_6_out, d_ff_11_q);
  and and_9 (and_9_out, d_ff_3_q, in_10);
  D_Flip_Flop d_ff_4 (.clk(clock_1_out), .D(xor_2_out), .Q(out_14));  // open: Qn, preset, en, reset
  D_Flip_Flop d_ff_5 (.clk(clock_1_out), .D(xor_3_out), .Q(out_15));  // open: Qn, preset, en, reset
  D_Flip_Flop d_ff_6 (.clk(clock_1_out), .D(xor_4_out), .Q(out_16));  // open: Qn, preset, en, reset
  D_Flip_Flop d_ff_7 (.clk(clock_1_out), .D(xor_5_out), .Q(out_17));  // open: Qn, preset, en, reset
  D_Flip_Flop d_ff_8 (.clk(clock_1_out), .D(d_ff_3_q), .Q(d_ff_8_q), .preset(and_9_out));  // open: Qn, en, reset
  and and_10 (and_10_out, d_ff_8_q, in_11);
  D_Flip_Flop d_ff_9 (.clk(clock_1_out), .D(d_ff_8_q), .Q(d_ff_9_q), .preset(and_10_out));  // open: Qn, en, reset
  and and_11 (and_11_out, d_ff_9_q, in_12);
  D_Flip_Flop d_ff_10 (.clk(clock_1_out), .D(d_ff_9_q), .Q(d_ff_10_q), .preset(and_11_out));  // open: Qn, en, reset
  and and_12 (and_12_out, d_ff_10_q, in_13);
  D_Flip_Flop d_ff_11 (.clk(clock_1_out), .D(d_ff_10_q), .Q(d_ff_11_q), .preset(and_12_out));  // open: Qn, en, reset
endmodule
