// Logisim project 先行进位的四位二进制并行加法器2.circ as structural Verilog: 1 circuit, main circuit main
module main (
  input  B3,
  input  A3,
  input  B2,
  input  A2,
  input  B1,
  input  A1,
  input  B0,
  input  A0,
  input  Co,
  output C4,
  output S3,
  output S2,
  output S1,
  output S0
);

  wire and_1_out, and_2_out, and_3_out, and_4_out, and_5_out, and_6_out, and_7_out, and_8_out, and_9_out,
       and_10_out, and_11_out, and_12_out, and_13_out, and_14_out, and_15_out, and_16_out, and_17_out,
       and_18_out, and_19_out, and_20_out, and_21_out, and_22_out, and_23_out, and_24_out, and_25_out,
       and_26_out, and_27_out, and_28_out, and_29_out, and_30_out, and_31_out, and_32_out, and_33_out,
       and_34_out, and_35_out, and_36_out, and_37_out, and_38_out, and_39_out, and_40_out, and_41_out,
       and_42_out, and_43_out, and_44_out, and_45_out, not_1_out, not_2_out, not_3_out, not_4_out, not_5_out,
       not_6_out, not_7_out, not_8_out, not_9_out, not_10_out, not_11_out, not_12_out, not_13_out,
       not_14_out, not_15_out, not_16_out, not_17_out, not_18_out, not_19_out, not_20_out, not_21_out,
       not_22_out, not_23_out, not_24_out, not_25_out, not_26_out, not_27_out, not_28_out, not_29_out,
       not_30_out, not_31_out, not_32_out, not_33_out, not_34_out, not_35_out, not_36_out, not_37_out,
       not_38_out, not_39_out, not_40_out, not_41_out, not_42_out, not_43_out, not_44_out, not_45_out,
       not_46_out, not_47_out, not_48_out, not_49_out, not_50_out, not_51_out, not_52_out, not_53_out,
       not_54_out, not_55_out, not_56_out, not_57_out, not_58_out, not_59_out, not_60_out, not_61_out,
       not_62_out, not_63_out, not_64_out, not_65_out, not_66_out, not_67_out, not_68_out, not_69_out,
       not_70_out, not_71_out, not_72_out, not_73_out, not_74_out, not_75_out, not_76_out;

  and and_1 (and_1_out, A3, A2, B1, A1);
  and and_2 (and_2_out, A3, B2, B1, A1);
  and and_3 (and_3_out, A3, B2, A2);
  and and_4 (and_4_out, B3, A2, B1, A1);
  and and_5 (and_5_out, B3, B2, B1, A1);
  and and_6 (and_6_out, B3, B2, A2);
  and and_7 (and_7_out, B3, A3);
  not not_1 (not_1_out, B3);
  not not_2 (not_2_out, A3);
  not not_3 (not_3_out, B3);
  not not_4 (not_4_out, A3);
  not not_5 (not_5_out, B3);
  not not_6 (not_6_out, A3);
  not not_7 (not_7_out, B3);
  not not_8 (not_8_out, B2);
  not not_9 (not_9_out, A2);
  not not_10 (not_10_out, B3);
  not not_11 (not_11_out, B2);
  not not_12 (not_12_out, B1);
  not not_13 (not_13_out, B3);
  not not_14 (not_14_out, B2);
  not not_15 (not_15_out, A1);
  not not_16 (not_16_out, B3);
  not not_17 (not_17_out, A2);
  not not_18 (not_18_out, B1);
  not not_19 (not_19_out, B3);
  not not_20 (not_20_out, A2);
  not not_21 (not_21_out, A1);
  not not_22 (not_22_out, A3);
  not not_23 (not_23_out, B2);
  not not_24 (not_24_out, A2);
  not not_25 (not_25_out, A3);
  not not_26 (not_26_out, B2);
  not not_27 (not_27_out, B1);
  not not_28 (not_28_out, A3);
  not not_29 (not_29_out, B2);
  not not_30 (not_30_out, A1);
  not not_31 (not_31_out, A3);
  not not_32 (not_32_out, A2);
  not not_33 (not_33_out, B1);
  not not_34 (not_34_out, A3);
  not not_35 (not_35_out, A2);
  not not_36 (not_36_out, A1);
  not not_37 (not_37_out, B2);
  not not_38 (not_38_out, A2);
  not not_39 (not_39_out, B2);
  not not_40 (not_40_out, B1);
  not not_41 (not_41_out, B2);
  not not_42 (not_42_out, A1);
  not not_43 (not_43_out, A2);
  not not_44 (not_44_out, B1);
  not not_45 (not_45_out, A2);
  not not_46 (not_46_out, A1);
  not not_47 (not_47_out, B1);
  not not_48 (not_48_out, A1);
  not not_49 (not_49_out, B1);
  not not_50 (not_50_out, A1);
  not not_51 (not_51_out, B1);
  not not_52 (not_52_out, A1);
  not not_53 (not_53_out, B1);
  not not_54 (not_54_out, B0);
  not not_55 (not_55_out, A0);
  not not_56 (not_56_out, B1);
  not not_57 (not_57_out, B0);
  not not_58 (not_58_out, Co);
  not not_59 (not_59_out, B1);
  not not_60 (not_60_out, A0);
  not not_61 (not_61_out, Co);
  not not_62 (not_62_out, A1);
  not not_63 (not_63_out, B0);
  not not_64 (not_64_out, A0);
  not not_65 (not_65_out, A1);
  not not_66 (not_66_out, B0);
  not not_67 (not_67_out, Co);
  not not_68 (not_68_out, A1);
  not not_69 (not_69_out, A0);
  not not_70 (not_70_out, Co);
  not not_71 (not_71_out, B0);
  not not_72 (not_72_out, A0);
  not not_73 (not_73_out, B0);
  not not_74 (not_74_out, Co);
  not not_75 (not_75_out, A0);
  not not_76 (not_76_out, Co);
  or or_1 (C4, and_1_out, and_2_out, and_3_out, and_4_out, and_5_out, and_6_out, and_7_out);
  and and_8 (and_8_out, not_1_out, not_2_out, A2, B1, A1);
  and and_9 (and_9_out, not_3_out, not_4_out, B2, B1, A1);
  and and_10 (and_10_out, not_5_out, not_6_out, B2, A2);
  and and_11 (and_11_out, not_7_out, A3, not_8_out, not_9_out);
  and and_12 (and_12_out, not_10_out, A3, not_11_out, not_12_out);
  and and_13 (and_13_out, not_13_out, A3, not_14_out, not_15_out);
  and and_14 (and_14_out, not_16_out, A3, not_17_out, not_18_out);
  and and_15 (and_15_out, not_19_out, A3, not_20_out, not_21_out);
  and and_16 (and_16_out, B3, not_22_out, not_23_out, not_24_out);
  and and_17 (and_17_out, B3, not_25_out, not_26_out, not_27_out);
  and and_18 (and_18_out, B3, not_28_out, not_29_out, not_30_out);
  and and_19 (and_19_out, B3, not_31_out, not_32_out, not_33_out);
  and and_20 (and_20_out, B3, not_34_out, not_35_out, not_36_out);
  and and_21 (and_21_out, B3, A3, A2, B1, A1);
  and and_22 (and_22_out, B3, A3, B2, B1, A1);
  and and_23 (and_23_out, B3, A3, B2, A2);
  and and_24 (and_24_out, not_37_out, not_38_out, B1, A1);
  and and_25 (and_25_out, not_39_out, A2, not_40_out);
  and and_26 (and_26_out, not_41_out, A2, not_42_out);
  and and_27 (and_27_out, B2, not_43_out, not_44_out);
  and and_28 (and_28_out, B2, not_45_out, not_46_out);
  and and_29 (and_29_out, B2, A2, B1, A1);
  and and_30 (and_30_out, not_47_out, not_48_out, A0, Co);
  and and_31 (and_31_out, not_49_out, not_50_out, B0, Co);
  and and_32 (and_32_out, not_51_out, not_52_out, B0, A0);
  and and_33 (and_33_out, not_53_out, A1, not_54_out, not_55_out);
  and and_34 (and_34_out, not_56_out, A1, not_57_out, not_58_out);
  and and_35 (and_35_out, not_59_out, A1, not_60_out, not_61_out);
  and and_36 (and_36_out, B1, not_62_out, not_63_out, not_64_out);
  and and_37 (and_37_out, B1, not_65_out, not_66_out, not_67_out);
  and and_38 (and_38_out, B1, not_68_out, not_69_out, not_70_out);
  and and_39 (and_39_out, B1, A1, A0, Co);
  and and_40 (and_40_out, B1, A1, B0, Co);
  and and_41 (and_41_out, B1, A1, B0, A0);
  and and_42 (and_42_out, not_71_out, not_72_out, Co);
  and and_43 (and_43_out, not_73_out, A0, not_74_out);
  and and_44 (and_44_out, B0, not_75_out, not_76_out);
  and and_45 (and_45_out, B0, A0, Co);
  or or_2 (S2, and_24_out, and_25_out, and_26_out, and_27_out, and_28_out, and_29_out);
  or or_3 (S1, and_30_out, and_31_out, and_32_out, and_33_out, and_34_out, and_35_out, and_36_out, and_37_out, and_38_out, and_39_out, and_40_out, and_41_out);
  or or_4 (S0, and_42_out, and_43_out, and_44_out, and_45_out);
  or or_5 (S3, and_8_out, and_9_out, and_10_out, and_11_out, and_12_out, and_13_out, and_14_out, and_15_out, and_16_out, and_17_out, and_18_out, and_19_out, and_20_out, and_21_out, and_22_out, and_23_out);
endmodule
